# Fritzing sketch circuit (saved by Fritzing 0.9.3b)
breadboards: 1

parts:
  Part1 = Arduino Uno (Rev3) - ICSP  # not connected
  LM358P = IC, DIP package, 8 pins [chip_label=IC]
  part = Resistor [tolerance=±5% resistance=220 package="0805 [SMD]"]
  PD = S1133 Si Photodiode [package="8mm Ceramic [THT]"]
  IRLED = LTE-302 [package=lte-302]
  R2 = Resistor [tolerance=±5% resistance=220 package="0805 [SMD]"]
  R3 = TRIMPOT [package=trimpot_tc33]
  LM358P1 = IC, DIP package, 8 pins [chip_label=IC]
  R5 = Resistor [tolerance=±5% resistance=220 package="0805 [SMD]"]
  R6 = Resistor [tolerance=±5% resistance=220 package="0805 [SMD]"]
  PD1 = S1133 Si Photodiode [package="8mm Ceramic [THT]"]
  IRLED1 = LTE-302 [package=lte-302]
  R7 = TRIMPOT [package=trimpot_tc33]
  LM358P2 = IC, DIP package, 8 pins [chip_label=IC]
  R8 = Resistor [tolerance=±5% resistance=220 package="0805 [SMD]"]
  R9 = Resistor [tolerance=±5% resistance=220 package="0805 [SMD]"]
  PD2 = S1133 Si Photodiode [package="8mm Ceramic [THT]"]
  IRLED2 = LTE-302 [package=lte-302]
  R10 = TRIMPOT [package=trimpot_tc33]

nets:
  N1: LM358P.pin4, part.Pin_0, PD.cathode
  N2: LM358P.pin5, R3.WIPER
  N3: IRLED.C, R2.Pin_0
  N4: LM358P1.pin4, R6.Pin_0, PD1.cathode
  N5: LM358P1.pin5, R7.WIPER
  N6: R5.Pin_0, IRLED1.C
  N7: LM358P2.pin4, R8.Pin_0, PD2.cathode
  N8: LM358P2.pin5, R10.WIPER
  N9: R9.Pin_0, IRLED2.C

// code stored in the sketch: driver.ino
int ins[] = {A0,A1,A2};
int outs[] = {8,9,10};
int warningLight = 7;
int offDelay = 500;
int loopTime = 10;
int states[] = {0, 0, 0};
int val = 0;
int times[] = {0, 0, 0};
float L = 20.0;
float maxSpeed = 40.0;
int warningDelay = 3000;
int curr = 0;
 
void setup() {
  // put your setup code here, to run once:
  Serial.begin(9600);
Serial.print("Setting Up...");
  pinMode(warningLight, OUTPUT);
  for(int i = 0; i <3; i++){
    pinMode(ins[i], INPUT);
    pinMode(outs[i], OUTPUT);
  }
}

void loop() {
  // put your main code here, to run repeatedly:
  for(int i = 0; i < 3; i++){
    val = analogRead(ins[i]);
    if(val > 40){
      turnOn(i);
      Serial.print("Obstacle\n");
      times[i] += loopTime;
//      Serial.print(times[i]);
//      Serial.print("\n");
      states[i] = offDelay;
    }
    else{
      //pin is off
      if(times[i] >= loopTime){
        //pin was just turned off
        float T = (float)times[i]/ 1000;
        float s = L/T;
        times[i] = 0;
       
        if (s > maxSpeed){
          Serial.print("SPEED EXCEEDED\n");
          digitalWrite(warningLight, HIGH);
          curr = warningDelay;
        }
      }
    }
  }

  if (curr <= 0){
    digitalWrite(warningLight, LOW);
  }
  else{
     curr -= loopTime;
  }
 
//  Serial.print(curr);
//  Serial.print("\n"); 
  for (int j = 0; j < 3; j++){
    if(states[j] <= 0){ 
      turnOff(j);
    }
    else{
      states[j] -= loopTime;
    }
  }
  delay(loopTime);
}

void turnOn(int index){
  digitalWrite(outs[index], HIGH);
}

void turnOff(int index){
  digitalWrite(outs[index], LOW);
}
